# Fritzing sketch climate_sensor (saved by Fritzing 0.9.3b)
breadboards: 1

parts:
  U1 = NodeMCU V1.0
  J1 = male pin header, 3 pins [form="♂ (male)"]

nets:
  N1: U1.D2, J1.pin1
  N2: U1.3V3, J1.pin2
  N3: U1.GND, J1.pin3

custom parts:
  NodeMCU V1.0: ESP8266 based NodeMCU
